# Fritzing sketch diseño_circuito_frizting (saved by Fritzing 0.9.3b)
breadboards: 1

parts:
  Espessif_Serial_Wifi_Modul_1 = ESP8266 ESP01 [part_number=ESP8266 package=THT]
  Componente1 = Arduino Uno (Rev3) - ICSP
  KY-1 = Keyes Relay [package=THT]
  WATER_PUMP1 = water pump/motor  # not connected
  DHT1 = DHT11 Humitidy and Temperature Sensor
  Capacitive_Soil_Moisture_Sensor1 = DFRobot Capacitive Soil Moisture Sensor V1.0 [part_number=SEN0193]
  A1 = Hanmatek HM305

nets:
  GND: Espessif_Serial_Wifi_Modul_1.GND, Componente1.GND, KY-1.ground
  N1: Espessif_Serial_Wifi_Modul_1.RXD, Componente1.D3_PWM
  N2: Espessif_Serial_Wifi_Modul_1.TXD, Componente1.D2
  VCC: Espessif_Serial_Wifi_Modul_1.VCC, Espessif_Serial_Wifi_Modul_1.CH_PD, Componente1.5V, KY-1.power, A1.Pin_2
  N3: Componente1.A0, Capacitive_Soil_Moisture_Sensor1.VCC
  N4: Componente1.D10_PWM/SS, DHT1.DATA
  N5: Componente1.D4, KY-1.signal
  N6: KY-1.NO, DHT1.VDD, Capacitive_Soil_Moisture_Sensor1.A, A1.Pin_1
  GND_2: DHT1.GND, Capacitive_Soil_Moisture_Sensor1.GND

custom parts:
  ESP8266 ESP01: Generic WiFi Module based on the ESP8266 with onboard PCB antenna and UART communications
  Keyes Relay: The Keyes 5V relay module is suitable for SCM development, home appliance control. It uses a 5V~12V TIL control signal which can control DC / AC signal.
  water pump/motor: WATER PUMP BY ARDUBLOCKTR
  DHT11 Humitidy and Temperature Sensor: DHT11 Humidity and Temperature Sensor
  DFRobot Capacitive Soil Moisture Sensor V1.0: DFRobot Capacitive Soil Moisture Sensor V1.0 This product measures soil moisture levels by capacitive sensing, rather than resistive sensing like other types of moisture sensor. It is made of a corrosion resistant material giving it a long service life. Insert it into soil and impress your friends with the real-time soil moisture data! The product includes an on-board voltage regulator which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
  Hanmatek HM305: DC Power Supply 30V5A HM305.
